# Fritzing sketch wort-warden-iteration-1 (saved by Fritzing 0.9.3b)
breadboards: 1

parts:
  WeMos_D1_Mini1 = WeMos D1 Mini
  GY1 = MPU-6050 Board GY-521 [form="♀ (female)" package=THT]

nets:
  N1: WeMos_D1_Mini1.5V, GY1.pin1
  N2: WeMos_D1_Mini1.D0, WeMos_D1_Mini1.RST
  N3: WeMos_D1_Mini1.D3, GY1.pin4
  N4: WeMos_D1_Mini1.D4, GY1.pin3
  N5: WeMos_D1_Mini1.G, GY1.pin2

notes:
  == Powered overUSB
  == via a powerbank

custom parts:
  WeMos D1 Mini: The D1 mini is a mini wifi board based on ESP-8266EX.
  MPU-6050 Board GY-521: Acelerometro y Giroscopio MPU-6050 Board GY-521
