# Fritzing sketch wort-warden (saved by Fritzing 0.9.3b)
breadboards: 1

parts:
  WeMos_D1_Mini1 = WeMos D1 Mini
  Part1 = MCP9808 High Accuracy I2C Temperature Sensor [part_number=1782]
  Part2 = TP4056 Charger
  GY1 = MPU-6050 Board GY-521 [form="♀ (female)" package=THT]
  U1 = LIPO-2000mAh [package=lipo-2000]
  U2 = SWITCH_SPDT [package=kps-1290]

nets:
  5V: WeMos_D1_Mini1.5V, Part1.VDD, Part2.BAT+, GY1.pin1, U1.+
  N1: WeMos_D1_Mini1.D0, WeMos_D1_Mini1.RST
  N2: WeMos_D1_Mini1.D1, Part1.SDA, GY1.pin4
  N3: WeMos_D1_Mini1.D2, Part1.SCL, GY1.pin3
  N4: WeMos_D1_Mini1.D4, U2.S
  N5: WeMos_D1_Mini1.G, Part1.GND, Part2.BAT-, GY1.pin2, U1.-, U2.O, U2.P

notes:
  Switch dev mode

custom parts:
  WeMos D1 Mini: The D1 mini is a mini wifi board based on ESP-8266EX.
  MCP9808 High Accuracy I2C Temperature Sensor: This I2C digital temperature sensor is one of the more accurate/precise we've ever seen, with a typical accuracy of ±0.25°C over the sensor's -40°C to +125°C range and precision of +0.0625°C. They work great with any microcontroller using standard i2c. There are 3 address pins so you can connect up to 8 to a single I2C bus without address collisions. Best of all, a wide voltage range makes is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
  MPU-6050 Board GY-521: Acelerometro y Giroscopio MPU-6050 Board GY-521
